# Fritzing sketch seven-segment-led-counter (saved by Fritzing 0.9.5d)
breadboards: 1

parts:
  パーツ1 = Arduino Uno (Rev3)
  OSL10561-IB = 7-Segment LED Display [package=THT]
  OSL10561-IB_2 = 7-Segment LED Display [package=THT]
  R1 = Resistor [tolerance=±5% resistance=100 package=THT]
  R2 = Resistor [tolerance=±5% resistance=100 package=THT]

nets:
  N1: パーツ1.D8, OSL10561-IB.cathodeF, OSL10561-IB_2.cathodeF
  N2: パーツ1.D9_PWM, OSL10561-IB.cathodeA, OSL10561-IB_2.cathodeA
  N3: パーツ1.D10_PWM/SS, OSL10561-IB.cathodeB, OSL10561-IB_2.cathodeB
  N4: パーツ1.D11_PWM/MOSI, OSL10561-IB.cathodeC, OSL10561-IB_2.cathodeC
  N5: パーツ1.D12/MISO, OSL10561-IB.cathodeD, OSL10561-IB_2.cathodeD
  N6: パーツ1.D13/SCK, OSL10561-IB.cathodeE, OSL10561-IB_2.cathodeE
  N7: パーツ1.D5_PWM, R2.Pin_0
  N8: パーツ1.D6_PWM, R1.Pin_0
  N9: パーツ1.D7, OSL10561-IB.cathodeG, OSL10561-IB_2.cathodeG
  N10: OSL10561-IB.commAnode#2, R1.Pin_1
  N11: OSL10561-IB_2.commAnode#2, R2.Pin_1
